// Digital circuit 4BitAdderBCD.dig as structural Verilog
module _4BitAdderBCD (
  input  [3:0] A,
  input  [3:0] B,
  input  Cin,
  output [3:0] Sum,
  output Cout
);

  wire and_1_out, or_1_out, xor_1_out;
  wire [1:0] _4bitadder_1_cout;
  wire [3:0] _4bitadder_1_sum, _4bitadder_2_sum;

  _4bitAdder _4bitadder_1 (.A(A), .B(B), .Cin(Cin), .Sum(_4bitadder_1_sum), .Cout(_4bitadder_1_cout[0]));
  or or_1 (or_1_out, _4bitadder_1_sum[1], _4bitadder_1_sum[2]);
  and and_1 (and_1_out, or_1_out, _4bitadder_1_sum[3]);
  or or_2 (_4bitadder_1_cout[1], and_1_out, _4bitadder_1_cout[0]);
  _4bitAdder _4bitadder_2 (.A(_4bitadder_1_sum), .B(4'b0110), .Cin(1'b0), .Sum(_4bitadder_2_sum));  // open: Cout
  xor xor_1 (xor_1_out, _4bitadder_1_cout[0], 1'b1);
  Multiplexer #(.Selector_Bits(2), .Bits(4)) multiplexer_1 (
    .sel(_4bitadder_1_cout), .in_0(_4bitadder_1_sum), .in_1(_4bitadder_2_sum), .in_2(_4bitadder_2_sum),
    .in_3(_4bitadder_1_sum), .out(Sum));
  Multiplexer #(.Selector_Bits(2)) multiplexer_2 (
    .sel(_4bitadder_1_cout), .in_0(_4bitadder_1_cout[0]), .in_1(_4bitadder_1_cout[0]), .in_2(xor_1_out),
    .in_3(_4bitadder_1_cout[0]), .out(Cout));
endmodule
