// Digital circuit 4bitAdder.dig as structural Verilog
module _4bitAdder (
  input  [3:0] A,
  input  [3:0] B,
  input  Cin,
  output [3:0] Sum,
  output Cout
);

  wire and_1_out, and_2_out, and_3_out, and_4_out, and_5_out, and_6_out, and_7_out, and_8_out, or_1_out,
       or_2_out, or_3_out, xor_1_out, xor_2_out, xor_3_out, xor_4_out;

  xor xor_1 (xor_1_out, A[0], B[0]);
  xor xor_2 (xor_2_out, A[1], B[1]);
  xor xor_3 (xor_3_out, A[2], B[2]);
  xor xor_4 (xor_4_out, A[3], B[3]);
  xor xor_5 (Sum[0], xor_1_out, Cin);
  and and_1 (and_1_out, xor_1_out, Cin);
  and and_2 (and_2_out, A[0], B[0]);
  xor xor_6 (Sum[1], xor_2_out, or_1_out);
  and and_3 (and_3_out, xor_2_out, or_1_out);
  and and_4 (and_4_out, A[1], B[1]);
  xor xor_7 (Sum[2], xor_3_out, or_2_out);
  and and_5 (and_5_out, xor_3_out, or_2_out);
  and and_6 (and_6_out, A[2], B[2]);
  xor xor_8 (Sum[3], xor_4_out, or_3_out);
  and and_7 (and_7_out, xor_4_out, or_3_out);
  and and_8 (and_8_out, A[3], B[3]);
  or or_1 (or_1_out, and_1_out, and_2_out);
  or or_2 (or_2_out, and_3_out, and_4_out);
  or or_3 (or_3_out, and_5_out, and_6_out);
  or or_4 (Cout, and_7_out, and_8_out);

  // Notes on the sheet:
  //   S0
  //   S1
  //   S2
  //   S3
  //   Cout
endmodule
