// Digital circuit calculator.dig as structural Verilog
module calculator (
  input  [3:0] DATA,
  input  DA,
  input  CLK,
  output [3:0] D0,
  output [3:0] D1,
  output [3:0] D2,
  output [3:0] D3,
  output [3:0] D4,
  output [3:0] D5,
  output [3:0] D6,
  output [3:0] D7
);

  wire _4bitadderbcd_1_cout, _4bitadderbcd_2_cout, _4bitadderbcd_3_cout, _4bitadderbcd_4_cout,
       _4bitadderbcd_5_cout, _4bitadderbcd_6_cout, _4bitadderbcd_7_cout, and_1_out, decoder_1_out_14,
       decoder_1_out_15, or_1_out, xor_1_out;
  wire [3:0] _4bitadderbcd_1_sum, _4bitadderbcd_2_sum, _4bitadderbcd_3_sum, _4bitadderbcd_4_sum,
       _4bitadderbcd_5_sum, _4bitadderbcd_6_sum, _4bitadderbcd_7_sum, _4bitadderbcd_8_sum, multiplexer_1_out,
       multiplexer_2_out, multiplexer_5_out, multiplexer_6_out, multiplexer_8_out, multiplexer_10_out,
       multiplexer_11_out, multiplexer_12_out, multiplexer_14_out, multiplexer_15_out, multiplexer_16_out,
       multiplexer_18_out, multiplexer_19_out, multiplexer_20_out, multiplexer_22_out, multiplexer_23_out,
       multiplexer_24_out, multiplexer_26_out, multiplexer_27_out, multiplexer_28_out, multiplexer_30_out,
       multiplexer_31_out, multiplexer_32_out, multiplexer_34_out, register_1_q, register_2_q, register_3_q,
       register_4_q, register_5_q, register_6_q, register_7_q, register_8_q, register_9_q, register_10_q,
       register_11_q, register_12_q, register_13_q, register_14_q, register_15_q, register_16_q;

  Decoder #(.Selector_Bits(4)) decoder_1 (
    .sel(DATA), .out_14(decoder_1_out_14), .out_15(decoder_1_out_15));  // open: out_0, out_1, out_2, out_3, out_4, out_5, out_6, out_7, out_8, out_9, out_10, out_11, out_12, out_13
  or or_1 (or_1_out, decoder_1_out_14, decoder_1_out_15);
  xor xor_1 (xor_1_out, DA, CLK);
  and and_1 (and_1_out, DA, xor_1_out);
  Multiplexer #(.Bits(4)) multiplexer_1 (.sel(or_1_out), .in_0(DATA), .in_1(4'b0000), .out(multiplexer_1_out));
  Multiplexer #(.Bits(4)) multiplexer_2 (
    .sel(decoder_1_out_14), .in_0(_4bitadderbcd_1_sum), .in_1(4'b0000), .out(multiplexer_2_out));
  Multiplexer multiplexer_3 (.sel(register_15_q[0]), .in_1(1'b0));  // open: in_0, out
  Register #(.Bits(4)) register_1 (.D(multiplexer_1_out), .C(CLK), .en(and_1_out), .Q(register_1_q));
  Register #(.Bits(4)) register_2 (.D(multiplexer_2_out), .C(CLK), .en(and_1_out), .Q(register_2_q));
  _4BitAdderBCD _4bitadderbcd_1 (
    .A(register_2_q), .B(multiplexer_5_out), .Cin(1'b0), .Sum(_4bitadderbcd_1_sum),
    .Cout(_4bitadderbcd_1_cout));
  Multiplexer #(.Bits(4)) multiplexer_4 (
    .sel(decoder_1_out_15), .in_0(register_1_q), .in_1(_4bitadderbcd_1_sum), .out(D0));
  Multiplexer #(.Bits(4)) multiplexer_5 (
    .sel(decoder_1_out_15), .in_0(4'b0000), .in_1(register_1_q), .out(multiplexer_5_out));
  Multiplexer #(.Bits(4)) multiplexer_6 (.sel(or_1_out), .in_0(register_1_q), .in_1(4'b0000), .out(multiplexer_6_out));
  Multiplexer multiplexer_7 ();  // open: sel, in_0, in_1, out
  Multiplexer #(.Bits(4)) multiplexer_8 (
    .sel(decoder_1_out_14), .in_0(_4bitadderbcd_2_sum), .in_1(4'b0000), .out(multiplexer_8_out));
  Register #(.Bits(4)) register_3 (.D(multiplexer_6_out), .C(CLK), .en(and_1_out), .Q(register_3_q));
  Register #(.Bits(4)) register_4 (.D(multiplexer_8_out), .C(CLK), .en(and_1_out), .Q(register_4_q));
  Multiplexer #(.Bits(4)) multiplexer_9 (
    .sel(decoder_1_out_15), .in_0(register_3_q), .in_1(_4bitadderbcd_2_sum), .out(D1));
  _4BitAdderBCD _4bitadderbcd_2 (
    .A(register_4_q), .B(multiplexer_10_out), .Cin(_4bitadderbcd_1_cout), .Sum(_4bitadderbcd_2_sum),
    .Cout(_4bitadderbcd_2_cout));
  Multiplexer #(.Bits(4)) multiplexer_10 (
    .sel(decoder_1_out_15), .in_0(4'b0000), .in_1(register_3_q), .out(multiplexer_10_out));
  Multiplexer #(.Bits(4)) multiplexer_11 (
    .sel(or_1_out), .in_0(register_3_q), .in_1(4'b0000), .out(multiplexer_11_out));
  Multiplexer #(.Bits(4)) multiplexer_12 (
    .sel(decoder_1_out_14), .in_0(_4bitadderbcd_3_sum), .in_1(4'b0000), .out(multiplexer_12_out));
  Register #(.Bits(4)) register_5 (.D(multiplexer_11_out), .C(CLK), .en(and_1_out), .Q(register_5_q));
  Register #(.Bits(4)) register_6 (.D(multiplexer_12_out), .C(CLK), .en(and_1_out), .Q(register_6_q));
  Multiplexer #(.Bits(4)) multiplexer_13 (
    .sel(decoder_1_out_15), .in_0(register_5_q), .in_1(_4bitadderbcd_3_sum), .out(D2));
  Multiplexer #(.Bits(4)) multiplexer_14 (
    .sel(decoder_1_out_15), .in_0(4'b0000), .in_1(register_5_q), .out(multiplexer_14_out));
  _4BitAdderBCD _4bitadderbcd_3 (
    .A(register_6_q), .B(multiplexer_14_out), .Cin(_4bitadderbcd_2_cout), .Sum(_4bitadderbcd_3_sum),
    .Cout(_4bitadderbcd_3_cout));
  Multiplexer #(.Bits(4)) multiplexer_15 (
    .sel(or_1_out), .in_0(register_5_q), .in_1(4'b0000), .out(multiplexer_15_out));
  Multiplexer #(.Bits(4)) multiplexer_16 (
    .sel(decoder_1_out_14), .in_0(_4bitadderbcd_4_sum), .in_1(4'b0000), .out(multiplexer_16_out));
  Register #(.Bits(4)) register_7 (.D(multiplexer_15_out), .C(CLK), .en(and_1_out), .Q(register_7_q));
  _4BitAdderBCD _4bitadderbcd_4 (
    .A(register_8_q), .B(multiplexer_18_out), .Cin(_4bitadderbcd_3_cout), .Sum(_4bitadderbcd_4_sum),
    .Cout(_4bitadderbcd_4_cout));
  Register #(.Bits(4)) register_8 (.D(multiplexer_16_out), .C(CLK), .en(and_1_out), .Q(register_8_q));
  Multiplexer #(.Bits(4)) multiplexer_17 (
    .sel(decoder_1_out_15), .in_0(register_7_q), .in_1(_4bitadderbcd_4_sum), .out(D3));
  Multiplexer #(.Bits(4)) multiplexer_18 (
    .sel(decoder_1_out_15), .in_0(4'b0000), .in_1(register_7_q), .out(multiplexer_18_out));
  Multiplexer #(.Bits(4)) multiplexer_19 (
    .sel(or_1_out), .in_0(register_7_q), .in_1(4'b0000), .out(multiplexer_19_out));
  Multiplexer #(.Bits(4)) multiplexer_20 (
    .sel(decoder_1_out_14), .in_0(_4bitadderbcd_5_sum), .in_1(4'b0000), .out(multiplexer_20_out));
  Register #(.Bits(4)) register_9 (.D(multiplexer_19_out), .C(CLK), .en(and_1_out), .Q(register_9_q));
  Register #(.Bits(4)) register_10 (.D(multiplexer_20_out), .C(CLK), .en(and_1_out), .Q(register_10_q));
  _4BitAdderBCD _4bitadderbcd_5 (
    .A(register_10_q), .B(multiplexer_22_out), .Cin(_4bitadderbcd_4_cout), .Sum(_4bitadderbcd_5_sum),
    .Cout(_4bitadderbcd_5_cout));
  Multiplexer #(.Bits(4)) multiplexer_21 (
    .sel(decoder_1_out_15), .in_0(register_9_q), .in_1(_4bitadderbcd_5_sum), .out(D4));
  Multiplexer #(.Bits(4)) multiplexer_22 (
    .sel(decoder_1_out_15), .in_0(4'b0000), .in_1(register_9_q), .out(multiplexer_22_out));
  Multiplexer #(.Bits(4)) multiplexer_23 (
    .sel(or_1_out), .in_0(register_9_q), .in_1(4'b0000), .out(multiplexer_23_out));
  Multiplexer #(.Bits(4)) multiplexer_24 (
    .sel(decoder_1_out_14), .in_0(_4bitadderbcd_6_sum), .in_1(4'b0000), .out(multiplexer_24_out));
  Register #(.Bits(4)) register_11 (.D(multiplexer_23_out), .C(CLK), .en(and_1_out), .Q(register_11_q));
  Register #(.Bits(4)) register_12 (.D(multiplexer_24_out), .C(CLK), .en(and_1_out), .Q(register_12_q));
  _4BitAdderBCD _4bitadderbcd_6 (
    .A(register_12_q), .B(multiplexer_26_out), .Cin(_4bitadderbcd_5_cout), .Sum(_4bitadderbcd_6_sum),
    .Cout(_4bitadderbcd_6_cout));
  Multiplexer #(.Bits(4)) multiplexer_25 (
    .sel(decoder_1_out_15), .in_0(register_11_q), .in_1(_4bitadderbcd_6_sum), .out(D5));
  Multiplexer #(.Bits(4)) multiplexer_26 (
    .sel(decoder_1_out_15), .in_0(4'b0000), .in_1(register_11_q), .out(multiplexer_26_out));
  Multiplexer #(.Bits(4)) multiplexer_27 (
    .sel(or_1_out), .in_0(register_11_q), .in_1(4'b0000), .out(multiplexer_27_out));
  Multiplexer #(.Bits(4)) multiplexer_28 (
    .sel(decoder_1_out_14), .in_0(_4bitadderbcd_7_sum), .in_1(4'b0000), .out(multiplexer_28_out));
  Register #(.Bits(4)) register_13 (.D(multiplexer_27_out), .C(CLK), .en(and_1_out), .Q(register_13_q));
  _4BitAdderBCD _4bitadderbcd_7 (
    .A(register_14_q), .B(multiplexer_30_out), .Cin(_4bitadderbcd_6_cout), .Sum(_4bitadderbcd_7_sum),
    .Cout(_4bitadderbcd_7_cout));
  Register #(.Bits(4)) register_14 (.D(multiplexer_28_out), .C(CLK), .en(and_1_out), .Q(register_14_q));
  Multiplexer #(.Bits(4)) multiplexer_29 (
    .sel(decoder_1_out_15), .in_0(register_13_q), .in_1(_4bitadderbcd_7_sum), .out(D6));
  Multiplexer #(.Bits(4)) multiplexer_30 (
    .sel(decoder_1_out_15), .in_0(4'b0000), .in_1(register_13_q), .out(multiplexer_30_out));
  Multiplexer #(.Bits(4)) multiplexer_31 (
    .sel(or_1_out), .in_0(register_13_q), .in_1(4'b0000), .out(multiplexer_31_out));
  Multiplexer #(.Bits(4)) multiplexer_32 (
    .sel(decoder_1_out_14), .in_0(_4bitadderbcd_8_sum), .in_1(4'b0000), .out(multiplexer_32_out));
  Register #(.Bits(4)) register_15 (.D(multiplexer_31_out), .C(CLK), .en(and_1_out), .Q(register_15_q));
  Register #(.Bits(4)) register_16 (.D(multiplexer_32_out), .C(CLK), .en(and_1_out), .Q(register_16_q));
  Multiplexer #(.Bits(4)) multiplexer_33 (
    .sel(decoder_1_out_15), .in_0(register_15_q), .in_1(_4bitadderbcd_8_sum), .out(D7));
  _4BitAdderBCD _4bitadderbcd_8 (
    .A(register_16_q), .B(multiplexer_34_out), .Cin(_4bitadderbcd_7_cout), .Sum(_4bitadderbcd_8_sum));  // open: Cout
  Multiplexer #(.Bits(4)) multiplexer_34 (
    .sel(decoder_1_out_15), .in_0(4'b0000), .in_1(register_15_q), .out(multiplexer_34_out));
  // Pins of 1 and 4 bits meet at register_15_q
  // Pins of 1 and 4 bits meet at 4'b1110
endmodule
